// Logisim project 8b_v1.circ as structural Verilog: 15 circuits, main circuit Mainboard
// R8b
module Register8b (
  input  [7:0] DIN,
  input  write,
  input  clk,
  input  areset,
  output [7:0] DOUT
);

  Register4b _0x0 (.DIN(DIN[3:0]), .write(write), .clk(clk), .areset(areset), .DOUT(DOUT[3:0]));
  Register4b _0x4 (.DIN(DIN[7:4]), .write(write), .clk(clk), .areset(areset), .DOUT(DOUT[7:4]));
endmodule

// +
module FullAdder (
  input  A,
  input  B,
  input  C,
  output S,
  output C_2
);

  wire and_1_out, and_2_out, and_3_out, or_1_out, xor_1_out;

  xor xor_1 (xor_1_out, A, B);
  and and_1 (and_1_out, A, B);
  and and_2 (and_2_out, A, C);
  and and_3 (and_3_out, B, C);
  xor xor_2 (S, xor_1_out, C);
  or or_1 (or_1_out, and_1_out, and_2_out);
  or or_2 (C_2, or_1_out, and_3_out);
endmodule

// +8b
module Adder8b (
  input  [7:0] A,
  input  [7:0] B,
  output [7:0] S,
  output C
);

  wire _0_c_2, _1_c_2, _2_c_2, _3_c_2, _4_c_2, _5_c_2, _6_c_2;

  FullAdder _0 (.A(A[0]), .B(B[0]), .C(1'b0), .S(S[0]), .C_2(_0_c_2));
  FullAdder _1 (.A(A[1]), .B(B[1]), .C(_0_c_2), .S(S[1]), .C_2(_1_c_2));
  FullAdder _2 (.A(A[2]), .B(B[2]), .C(_1_c_2), .S(S[2]), .C_2(_2_c_2));
  FullAdder _3 (.A(A[3]), .B(B[3]), .C(_2_c_2), .S(S[3]), .C_2(_3_c_2));
  FullAdder _4 (.A(A[4]), .B(B[4]), .C(_3_c_2), .S(S[4]), .C_2(_4_c_2));
  FullAdder _5 (.A(A[5]), .B(B[5]), .C(_4_c_2), .S(S[5]), .C_2(_5_c_2));
  FullAdder _6 (.A(A[6]), .B(B[6]), .C(_5_c_2), .S(S[6]), .C_2(_6_c_2));
  FullAdder _7 (.A(A[7]), .B(B[7]), .C(_6_c_2), .S(S[7]), .C_2(C));
endmodule

module RAM (
  input  [7:0] DIN,
  input  [3:0] addr,
  input  write,
  input  clk,
  input  areset,
  output [7:0] DOUT,
  output [7:0] _0x0,
  output [7:0] _0x1,
  output [7:0] _0x2,
  output [7:0] _0x3,
  output [7:0] _0x4,
  output [7:0] _0x5,
  output [7:0] _0x6,
  output [7:0] _0x7,
  output [7:0] _0x8,
  output [7:0] _0x9,
  output [7:0] _0xA,
  output [7:0] _0xB,
  output [7:0] _0xC,
  output [7:0] _0xD,
  output [7:0] _0xE,
  output [7:0] _0xF
);

  wire demultiplexer_1_out0, demultiplexer_1_out1, demultiplexer_1_out2, demultiplexer_1_out3,
       demultiplexer_1_out4, demultiplexer_1_out5, demultiplexer_1_out6, demultiplexer_1_out7,
       demultiplexer_1_out8, demultiplexer_1_out9, demultiplexer_1_out10, demultiplexer_1_out11,
       demultiplexer_1_out12, demultiplexer_1_out13, demultiplexer_1_out14, demultiplexer_1_out15;

  Demultiplexer #(.select(4)) demultiplexer_1 (
    .out0(demultiplexer_1_out0), .out1(demultiplexer_1_out1), .out2(demultiplexer_1_out2),
    .out3(demultiplexer_1_out3), .out4(demultiplexer_1_out4), .out5(demultiplexer_1_out5),
    .out6(demultiplexer_1_out6), .out7(demultiplexer_1_out7), .out8(demultiplexer_1_out8),
    .out9(demultiplexer_1_out9), .out10(demultiplexer_1_out10), .out11(demultiplexer_1_out11),
    .out12(demultiplexer_1_out12), .out13(demultiplexer_1_out13), .out14(demultiplexer_1_out14),
    .out15(demultiplexer_1_out15), .in(write), .sel(addr), .en(1'b1));
  Register8b u__0x0 (.DIN(DIN), .write(demultiplexer_1_out0), .clk(clk), .areset(areset), .DOUT(_0x0));
  Register8b u__0x1 (.DIN(DIN), .write(demultiplexer_1_out1), .clk(clk), .areset(areset), .DOUT(_0x1));
  Register8b u__0x2 (.DIN(DIN), .write(demultiplexer_1_out2), .clk(clk), .areset(areset), .DOUT(_0x2));
  Register8b u__0x3 (.DIN(DIN), .write(demultiplexer_1_out3), .clk(clk), .areset(areset), .DOUT(_0x3));
  Register8b u__0x4 (.DIN(DIN), .write(demultiplexer_1_out4), .clk(clk), .areset(areset), .DOUT(_0x4));
  Register8b u__0x5 (.DIN(DIN), .write(demultiplexer_1_out5), .clk(clk), .areset(areset), .DOUT(_0x5));
  Register8b u__0x6 (.DIN(DIN), .write(demultiplexer_1_out6), .clk(clk), .areset(areset), .DOUT(_0x6));
  Register8b u__0x7 (.DIN(DIN), .write(demultiplexer_1_out7), .clk(clk), .areset(areset), .DOUT(_0x7));
  Register8b u__0x8 (.DIN(DIN), .write(demultiplexer_1_out8), .clk(clk), .areset(areset), .DOUT(_0x8));
  Register8b u__0x9 (.DIN(DIN), .write(demultiplexer_1_out9), .clk(clk), .areset(areset), .DOUT(_0x9));
  Register8b u__0xA (.DIN(DIN), .write(demultiplexer_1_out10), .clk(clk), .areset(areset), .DOUT(_0xA));
  Register8b u__0xB (.DIN(DIN), .write(demultiplexer_1_out11), .clk(clk), .areset(areset), .DOUT(_0xB));
  Register8b u__0xC (.DIN(DIN), .write(demultiplexer_1_out12), .clk(clk), .areset(areset), .DOUT(_0xC));
  Register8b u__0xD (.DIN(DIN), .write(demultiplexer_1_out13), .clk(clk), .areset(areset), .DOUT(_0xD));
  Register8b u__0xE (.DIN(DIN), .write(demultiplexer_1_out14), .clk(clk), .areset(areset), .DOUT(_0xE));
  Register8b u__0xF (.DIN(DIN), .write(demultiplexer_1_out15), .clk(clk), .areset(areset), .DOUT(_0xF));
  Multiplexer #(.select(4), .width(8)) multiplexer_1 (
    .in0(_0x0), .in1(_0x1), .in2(_0x2), .in3(_0x3), .in4(_0x4), .in5(_0x5), .in6(_0x6), .in7(_0x7),
    .in8(_0x8), .in9(_0x9), .in10(_0xA), .in11(_0xB), .in12(_0xC), .in13(_0xD), .in14(_0xE), .in15(_0xF),
    .out(DOUT), .sel(addr), .en(1'b1));
endmodule

module PC (
  input  count,
  input  clk,
  input  areset,
  output [3:0] PC
);

  wire and_1_out;
  wire [3:0] adder4b_1_s;

  Register4b register4b_1 (.DIN(adder4b_1_s), .clk(and_1_out), .areset(areset), .DOUT(PC));  // open: write
  Adder4b adder4b_1 (.A(PC), .B(4'b0001), .S(adder4b_1_s));  // open: C
  and and_1 (and_1_out, count, clk);
endmodule

// +4b
module Adder4b (
  input  [3:0] A,
  input  [3:0] B,
  output [3:0] S,
  output C
);

  wire _0_c_2, _1_c_2, _2_c_2;

  FullAdder _0 (.A(A[0]), .B(B[0]), .C(1'b0), .S(S[0]), .C_2(_0_c_2));
  FullAdder _1 (.A(A[1]), .B(B[1]), .C(_0_c_2), .S(S[1]), .C_2(_1_c_2));
  FullAdder _2 (.A(A[2]), .B(B[2]), .C(_1_c_2), .S(S[2]), .C_2(_2_c_2));
  FullAdder _3 (.A(A[3]), .B(B[3]), .C(_2_c_2), .S(S[3]), .C_2(C));
endmodule

// R4b
module Register4b (
  input  [3:0] DIN,
  input  write,
  input  clk,
  input  areset,
  output [3:0] DOUT
);

  D_Flip_Flop _0x0 (.clk(clk), .D(DIN[0]), .Q(DOUT[0]), .en(write), .reset(areset));  // open: Qn, preset
  D_Flip_Flop _0x1 (.clk(clk), .D(DIN[1]), .Q(DOUT[1]), .en(write), .reset(areset));  // open: Qn, preset
  D_Flip_Flop _0x2 (.clk(clk), .D(DIN[2]), .Q(DOUT[2]), .en(write), .reset(areset));  // open: Qn, preset
  D_Flip_Flop _0x3 (.clk(clk), .D(DIN[3]), .Q(DOUT[3]), .en(write), .reset(areset));  // open: Qn, preset
endmodule

module CPU (
  input  [7:0] DIN,
  input  clk,
  input  areset,
  output [7:0] DOUT,
  output [7:0] IR,
  output [3:0] PC,
  output [3:0] ADDR,
  output [1:0] Rd,
  output write,
  output [1:0] Rs,
  output [1:0] Rt,
  output [7:0] R0,
  output [7:0] R1,
  output [7:0] R2,
  output [7:0] R3,
  output [2:0] state
);

  wire nsl_1_increment_pc, nsl_1_sel_ram_addr, nsl_1_sel_rd, nsl_1_sel_rs, nsl_1_write_ir,
       nsl_1_write_register;
  wire [7:0] adder8b_1_s, multiplexer_1_out, registerfile_1_dout_b;

  Multiplexer #(.width(8)) multiplexer_1 (
    .in0(DIN), .in1(adder8b_1_s), .out(multiplexer_1_out), .sel(nsl_1_sel_rd), .en(1'b1));
  Multiplexer #(.width(2)) multiplexer_2 (.in0(IR[3:2]), .in1(IR[5:4]), .out(Rs), .sel(nsl_1_sel_rs), .en(1'b1));
  RegisterFile registerfile_1 (
    .DIN(multiplexer_1_out), .addr_DIN(IR[3:2]), .DOUT_A(DOUT), .clk(clk), .areset(areset),
    .DOUT_B(registerfile_1_dout_b), .addr_DOUT_A(Rs), .addr_DOUT_B(IR[7:6]), .write(nsl_1_write_register),
    .R0(R0), .R2(R1), .R1(R2), .R3(R3));
  Register8b u_IR (.DIN(DIN), .write(nsl_1_write_ir), .clk(clk), .areset(areset), .DOUT(IR));
  Adder8b adder8b_1 (.A(DOUT), .B(registerfile_1_dout_b), .S(adder8b_1_s));  // open: C
  NSL nsl_1 (
    .instruction(IR[1:0]), .state(state), .sel_Rd(nsl_1_sel_rd), .sel_Rs(nsl_1_sel_rs),
    .write_Register(nsl_1_write_register), .write_IR(nsl_1_write_ir), .increment_PC(nsl_1_increment_pc),
    .sel_RAM_addr(nsl_1_sel_ram_addr), .write_RAM(write), .clk(clk), .areset(areset));
  PC pc_1 (.count(nsl_1_increment_pc), .clk(clk), .areset(areset), .PC(PC));
  Multiplexer #(.width(4)) multiplexer_3 (.in0(PC), .in1(IR[7:4]), .out(ADDR), .sel(nsl_1_sel_ram_addr), .en(1'b1));

  assign Rd = IR[3:2];
  assign Rt = IR[7:6];
endmodule

module NSL (
  input  [1:0] instruction,
  input  clk,
  input  areset,
  output sel_Rd,
  output sel_Rs,
  output write_Register,
  output write_IR,
  output increment_PC,
  output sel_RAM_addr,
  output write_RAM,
  output [2:0] state
);

  wire decoder_1_out4, or_1_out;
  wire [2:0] adder3b_1_s, instructiontostate_1_state, multiplexer_1_out, multiplexer_2_out;

  Adder3b adder3b_1 (.A(3'b001), .B(state), .S(adder3b_1_s));  // open: C
  // Probe on instructiontostate_1_state
  InstructionToState instructiontostate_1 (.Instruction(instruction), .State(instructiontostate_1_state));
  Multiplexer #(.width(3), .enable("false")) multiplexer_1 (
    .in0(adder3b_1_s), .in1(instructiontostate_1_state), .out(multiplexer_1_out), .sel(increment_PC));
  Multiplexer #(.width(3), .enable("false")) multiplexer_2 (
    .in0(multiplexer_1_out), .in1(3'b000), .out(multiplexer_2_out), .sel(or_1_out));
  Register3b u_State (.DIN(multiplexer_2_out), .write(1'b1), .clk(clk), .areset(areset), .DOUT(state));
  Decoder #(.select(3), .enable("false")) decoder_1 (
    .out0(write_IR), .out1(increment_PC), .out3(sel_Rd), .out4(decoder_1_out4), .out5(write_RAM), .sel(state));  // open: out2, out6, out7
  or or_1 (or_1_out, sel_Rd, decoder_1_out4, write_RAM);
  or or_2 (write_Register, sel_Rd, decoder_1_out4);
  or or_3 (sel_RAM_addr, decoder_1_out4, write_RAM);

  assign sel_Rs = sel_Rd;
endmodule

// RegFile
module RegisterFile (
  input  [1:0] addr_DIN,
  input  [1:0] addr_DOUT_A,
  input  [1:0] addr_DOUT_B,
  input  [7:0] DIN,
  input  write,
  input  clk,
  input  areset,
  output [7:0] DOUT_A,
  output [7:0] DOUT_B,
  output [7:0] R0,
  output [7:0] R2,
  output [7:0] R1,
  output [7:0] R3
);

  wire demultiplexer_1_out0, demultiplexer_1_out1, demultiplexer_1_out2, demultiplexer_1_out3;

  Demultiplexer #(.select(2)) demultiplexer_1 (
    .out0(demultiplexer_1_out0), .out1(demultiplexer_1_out1), .out2(demultiplexer_1_out2),
    .out3(demultiplexer_1_out3), .in(write), .sel(addr_DIN), .en(1'b1));
  Register8b _0x0 (.DIN(DIN), .write(demultiplexer_1_out0), .clk(clk), .areset(areset), .DOUT(R0));
  Register8b _0x1 (.DIN(DIN), .write(demultiplexer_1_out1), .clk(clk), .areset(areset), .DOUT(R1));
  Register8b _0x2 (.DIN(DIN), .write(demultiplexer_1_out2), .clk(clk), .areset(areset), .DOUT(R2));
  Register8b _0x3 (.DIN(DIN), .write(demultiplexer_1_out3), .clk(clk), .areset(areset), .DOUT(R3));
  Multiplexer #(.select(2), .width(8)) multiplexer_1 (
    .in0(R0), .in1(R1), .in2(R2), .in3(R3), .out(DOUT_A), .sel(addr_DOUT_A), .en(1'b1));
  Multiplexer #(.select(2), .width(8)) multiplexer_2 (
    .in0(R0), .in1(R1), .in2(R2), .in3(R3), .out(DOUT_B), .sel(addr_DOUT_B), .en(1'b1));
endmodule

// R3b
module Register3b (
  input  [2:0] DIN,
  input  write,
  input  clk,
  input  areset,
  output [2:0] DOUT
);

  D_Flip_Flop _0x0 (.clk(clk), .D(DIN[0]), .Q(DOUT[0]), .en(write), .reset(areset));  // open: Qn, preset
  D_Flip_Flop _0x1 (.clk(clk), .D(DIN[1]), .Q(DOUT[1]), .en(write), .reset(areset));  // open: Qn, preset
  D_Flip_Flop _0x2 (.clk(clk), .D(DIN[2]), .Q(DOUT[2]), .en(write), .reset(areset));  // open: Qn, preset
endmodule

// ITS
module InstructionToState (
  input  [1:0] Instruction,
  output [2:0] State
);

  not not_1 (State[1], Instruction[1]);

  assign {State[2], State[0]} = Instruction;
endmodule

module Mainboard (
  input  cpu_clk,
  input  areset
);

  wire and_1_out, clk_out, cpu_1_write, Load_out, loader_1_write_2;
  wire [1:0] cpu_1_rd, cpu_1_rs, cpu_1_rt;
  wire [2:0] cpu_1_state;
  wire [3:0] cpu_1_addr, cpu_1_pc, loader_1_addr_2, loader_1_rom_a;
  wire [7:0] cpu_1_dout, cpu_1_ir, cpu_1_r0, cpu_1_r1, cpu_1_r2, cpu_1_r3, loader_1_din, loader_1_din_2,
       ram_1__0x0, ram_1__0x1, ram_1__0x2, ram_1__0x3, ram_1__0x4, ram_1__0x5, ram_1__0x6, ram_1__0x7,
       ram_1__0x8, ram_1__0x9, ram_1__0xa, ram_1__0xb, ram_1__0xc, ram_1__0xd, ram_1__0xe, ram_1__0xf,
       ram_1_dout, rom_1_data;

  // Probe on cpu_1_ir
  // Probe on cpu_1_pc
  // Probe on cpu_1_rd
  // Probe on cpu_1_rs
  // Probe on cpu_1_rt
  // Probe on cpu_1_r0
  // Probe on cpu_1_r1
  // Probe on cpu_1_r2
  // Probe on cpu_1_r3
  // Probe on cpu_1_state
  // Probe on loader_1_din
  CPU cpu_1 (
    .IR(cpu_1_ir), .PC(cpu_1_pc), .Rd(cpu_1_rd), .Rs(cpu_1_rs), .Rt(cpu_1_rt), .R0(cpu_1_r0), .R1(cpu_1_r1),
    .R2(cpu_1_r2), .R3(cpu_1_r3), .state(cpu_1_state), .DIN(loader_1_din), .DOUT(cpu_1_dout),
    .ADDR(cpu_1_addr), .write(cpu_1_write), .clk(and_1_out), .areset(areset));
  and and_1 (and_1_out, clk_out, cpu_clk);
  // Probe on cpu_1_write
  // Probe on cpu_1_addr
  // Probe on cpu_1_dout
  // Probe on ram_1_dout
  Loader loader_1 (
    .DIN(loader_1_din), .DOUT_2(cpu_1_dout), .addr(cpu_1_addr), .write(cpu_1_write), .DOUT(ram_1_dout),
    .DIN_2(loader_1_din_2), .addr_2(loader_1_addr_2), .write_2(loader_1_write_2), .ROM_A(loader_1_rom_a),
    .ROM_D(rom_1_data), .clk(clk_out), .areset(areset), .load(Load_out));
  Button Load (.out(Load_out));
  Clock clk (.out(clk_out));
  // Probe on loader_1_addr_2
  // Probe on loader_1_din_2
  // Probe on loader_1_write_2
  RAM ram_1 (
    .DIN(loader_1_din_2), .DOUT(ram_1_dout), .addr(loader_1_addr_2), .write(loader_1_write_2),
    ._0x0(ram_1__0x0), ._0x1(ram_1__0x1), ._0x2(ram_1__0x2), ._0x3(ram_1__0x3), ._0x4(ram_1__0x4),
    ._0x5(ram_1__0x5), ._0x6(ram_1__0x6), ._0x7(ram_1__0x7), ._0x8(ram_1__0x8), ._0x9(ram_1__0x9),
    ._0xA(ram_1__0xa), ._0xB(ram_1__0xb), ._0xC(ram_1__0xc), ._0xD(ram_1__0xd), ._0xE(ram_1__0xe),
    ._0xF(ram_1__0xf), .clk(clk_out), .areset(areset));
  // Probe on ram_1__0x0
  // Probe on ram_1__0x1
  // Probe on ram_1__0x2
  // Probe on ram_1__0x3
  // Probe on ram_1__0x4
  // Probe on ram_1__0x5
  // Probe on ram_1__0x6
  // Probe on ram_1__0x7
  // Probe on ram_1__0x8
  // Probe on ram_1__0x9
  // Probe on ram_1__0xa
  // Probe on ram_1__0xb
  // Probe on ram_1__0xc
  // Probe on ram_1__0xd
  // Probe on ram_1__0xe
  // Probe on ram_1__0xf
  ROM #(.addrWidth(4)) rom_1 (.addr(loader_1_rom_a), .data(rom_1_data));  // open: sel

  // Notes on the sheet:
  //   contents of rom_1 (hex, n*v repeats v):
  //   9b ac 76 fb 77 fc 77 fd 77 fe 0 3 a
endmodule

// +3b
module Adder3b (
  input  [2:0] A,
  input  [2:0] B,
  output [2:0] S,
  output C
);

  wire _0_c_2, _1_c_2;

  FullAdder _0 (.A(A[0]), .B(B[0]), .C(1'b0), .S(S[0]), .C_2(_0_c_2));
  FullAdder _1 (.A(A[1]), .B(B[1]), .C(_0_c_2), .S(S[1]), .C_2(_1_c_2));
  FullAdder _2 (.A(A[2]), .B(B[2]), .C(_1_c_2), .S(S[2]), .C_2(C));
endmodule

module Loader (
  input  [7:0] ROM_D,
  input  [7:0] DOUT,
  input  [7:0] DOUT_2,
  input  [3:0] addr,
  input  write,
  input  clk,
  input  areset,
  input  load,
  output [3:0] ROM_A,
  output [7:0] DIN,
  output [7:0] DIN_2,
  output [3:0] addr_2,
  output write_2
);

  wire counter_1_carry, j_k_ff_1_q;

  Counter #(.width(4), .max('hf)) counter_1 (
    .count(j_k_ff_1_q), .Q(ROM_A), .carry(counter_1_carry), .clk(clk), .clr(areset));  // open: load, D
  J_K_Flip_Flop j_k_ff_1 (
    .J(load), .clk(clk), .K(counter_1_carry), .Q(j_k_ff_1_q), .en(1'b1), .reset(areset));  // open: Qn, preset
  Multiplexer #(.width(8), .enable("false")) multiplexer_1 (.in0(DOUT_2), .in1(ROM_D), .out(DIN_2), .sel(j_k_ff_1_q));
  Multiplexer #(.width(4), .enable("false")) multiplexer_2 (.in0(addr), .in1(ROM_A), .out(addr_2), .sel(j_k_ff_1_q));
  or or_1 (write_2, write, j_k_ff_1_q);

  assign DIN = DOUT;
endmodule
